# Fritzing sketch CWKeyer (saved by Fritzing 1.0.4)
circuit board: 8.46667cm x 5.64444cm
breadboards: 1

parts:
  U1 = NodeMCU V3.0
  R1 = 12mm Trimmer Potentiometer (Large) [maximum_resistance=10kΩ knob_status=50% power=0.5W package=THT]
  Display = male pin header, 4 pins [form="♂ (male)"]
  Encoder = male pin header, 5 pins [form="♂ (male)"]
  Battery = male pin header, 2 pins [form="♂ (male)"]
  Keyer = male pin header, 3 pins [form="♂ (male)"]
  Speaker = male pin header, 3 pins [form="♂ (male)"]
  J1 = Piezo Speaker

nets:
  N1: U1.D0, Encoder.pin4
  N2: U1.D1, Display.pin1
  N3: U1.D2, Display.pin2
  N4: U1.D3, Encoder.pin2
  N5: U1.D4, Encoder.pin3
  N6: U1.3V3, Display.pin3, Encoder.pin5
  N7: U1.GND, R1.leg1, Display.pin4, Encoder.pin1, Battery.pin2, Keyer.pin1, Speaker.pin1, J1.pin2
  N8: U1.D5, R1.leg2
  N9: U1.D6, Keyer.pin2
  N10: U1.D7, Keyer.pin3
  N11: U1.D8, J1.pin1
  N12: U1.Vin, Battery.pin1
  N13: R1.wiper, Speaker.pin2, Speaker.pin3

custom parts:
  NodeMCU V3.0: ESP8266 based NodeMCU
